# Fritzing sketch RobotSchematic (saved by Fritzing 0.9.3b)
breadboards: 2

parts:
  Part1 = Arduino Uno (Rev3) - ICSP
  Adafruit_HUZZAH_ESP8266_Breakout1 = Adafruit HUZZAH ESP8266 Breakout [part_number=2471]
  M1 = DC Motor
  M2 = DC Motor
  Part2 = Adafruit TB6612 DC and Stepper Motor Driver [part_number="Adafruit #2448"]
  R1 = Resistor [tolerance=±5% resistance=220 package=THT]
  R2 = Resistor [tolerance=±5% resistance=220 package=THT]
  R3 = Resistor [tolerance=±5% resistance=220 package=THT]
  LED1 = LED - 5mm [color="Green (565nm)" package="5 mm [THT]"]
  LED2 = LED - 5mm [color="Blue (470nm)" package="5 mm [THT]"]
  LED3 = LED - 5mm [color="Red (635nm)" package="5 mm [THT]"]
  J1 = Camdenboss CTB0158-4 [part_number=CTB0158-4 package=THT]
  VCC1 = Battery block 9V
  VCC2 = Battery block 9V
  S1 = SPST Switch [package=switch-spdt_lock.007s]
  S2 = SPST Switch [package=switch-spdt_lock.007s]
  R4 = Resistor [tolerance=±5% resistance=220 package=THT]
  R5 = Resistor [tolerance=±5% resistance=220 package=THT]
  LED4 = LED - 5mm [color="Green (565nm)" package="5 mm [THT]"]
  LED5 = LED - 5mm [color="Red (635nm)" package="5 mm [THT]"]
  IC1 = Voltage Regulator [package=to-220-alt]
  C1 = Electrolytic Capacitor [capacitance=2.2µF package="0405 [SMD, electrolytic]"]
  C3 = Ceramic Capacitor [capacitance=0.1µF package="0603 [SMD, multilayer]"]
  R6 = Photocell (LDR) [package=THT]
  R7 = TRIMPOT [package=trimpot_pth_s3_lock]

nets:
  N1: Part1.A5/SCL, R6.pin_0, R7.CW
  N2: Part1.5V, Adafruit_HUZZAH_ESP8266_Breakout1.VBat, R6.pin_1
  N3: Part1.D8, Part2.STBY
  N4: Part1.D9_PWM, Part2.BIN1
  N5: Part1.D10_PWM/SS, Part2.BIN2
  N6: Part1.D11_PWM/MOSI, Part2.PWMB
  N7: Part1.D12/MISO, LED3.anode
  N8: Part1.D13/SCK, LED2.anode
  N9: Part1.D2, Adafruit_HUZZAH_ESP8266_Breakout1.TX
  N10: Part1.D3_PWM, Adafruit_HUZZAH_ESP8266_Breakout1.RX
  N11: Part1.D4, LED1.anode
  N12: Part1.D5_PWM, Part2.PWMA
  N13: Part1.D6_PWM, Part2.AIN2
  N14: Part1.D7, Part2.AIN1
  3V3: Part1.3V3, Part2.VCC
  GND: Part1.GND, Adafruit_HUZZAH_ESP8266_Breakout1.GND, Part2.GND, R1.Pin_1, R2.Pin_1, R3.Pin_1, J1.pin1, J1.pin3, R4.Pin_1, IC1.IN, C1.-, C3.0
  N15: Part1.VIN, IC1.OUT, C3.1
  N16: M1.pin_1, Part2.MOTORA1
  N17: M1.pin_2, Part2.MOTORA2
  N18: M2.pin_1, Part2.MOTORB2
  N19: M2.pin_2, Part2.MOTORB1
  N20: Part2.PWRIN, S2.P, LED5.anode
  N21: R1.Pin_0, LED2.cathode
  N22: R2.Pin_0, LED1.cathode
  N23: R3.Pin_0, LED3.cathode
  N24: J1.pin2, S1.S
  N25: J1.pin4, S2.O, R5.Pin_1
  N26: J1.terminal_1, VCC2.-
  N27: J1.terminal_2, VCC2.+
  N28: J1.terminal_3, VCC1.-
  N29: J1.terminal_4, VCC1.+
  N30: S1.O, S1.P, R4.Pin_0, LED4.cathode, LED4.anode, IC1.GND, C1.+
  N31: S2.S, R5.Pin_0, LED5.cathode

custom parts:
  Adafruit TB6612 DC and Stepper Motor Driver: Spin two DC motors, step one bi-polar or uni-polar stepper, or fire off two solenoids with 1.2A per channel using the TB6612. These are perhaps better known as "the drivers in our assembled Adafruit Motorshield or Motor HAT." We really like these dual H-bridges, so if you want to control motors without a shield or HAT these are easy to include on any solderless breadboard or perma-proto.
